// Logisim project 1607058.circ as structural Verilog: 1 circuit, main circuit main
module main (
  input  A,
  input  in_2,
  input  C,
  input  D,
  output P,
  output Q,
  output R,
  output S
);

  wire and_1_out, and_2_out, and_3_out, and_4_out, and_5_out, and_6_out, not_1_out, not_2_out, not_3_out;

  not not_1 (not_1_out, D);
  not not_2 (not_2_out, in_2);
  not not_3 (not_3_out, C);
  and and_1 (and_1_out, in_2, C);
  and and_2 (and_2_out, in_2, D);
  and and_3 (and_3_out, not_1_out, in_2);
  and and_4 (and_4_out, not_2_out, C);
  and and_5 (and_5_out, not_3_out, D, in_2);
  and and_6 (and_6_out, not_3_out, in_2);
  or or_1 (P, and_1_out, and_2_out, A);
  or or_2 (Q, and_3_out, and_1_out, A);
  or or_3 (R, and_4_out, A, and_5_out);
  xor xor_1 (S, and_6_out, D);

  // Notes on the sheet:
  //   B
  //   BC
  //   BD
  //   BD'
  //   B'C
  //   BC'D
  //   BC'
  //   D
  //   A+BD+BC
  //   A+BC+BD'
  //   A+B'C+BC'D
  //   BC' XOR D
endmodule
